# Fritzing sketch A4 schematic 2 (saved by Fritzing 0.9.3b)
breadboards: 1

parts:
  Part1 = Arduino Uno (Rev3)
  R1 = Photocell (LDR) [package=THT]
  R2 = Resistor [tolerance=±5% resistance=220 package=THT]
  R3 = Resistor [tolerance=±5% resistance=220 package=THT]
  Q1 = NPN-Transistor [package="TO92 [THT]"]
  RGB_Strip_LED2 = RGB Strip LED
  Power_plug1 = Power plug

nets:
  N1: Part1.A0, R1.pin_1, R2.Pin_0
  N2: Part1.D9_PWM, R3.Pin_1
  GND: Part1.GND, R2.Pin_1, Q1.E, Power_plug1.GND
  N3: Part1.5V, R1.pin_0
  N4: R3.Pin_0, Q1.B
  N5: Q1.C, RGB_Strip_LED2.Common_Connect#4
  N6: RGB_Strip_LED2.Red_Connect#6, Power_plug1.VCC

custom parts:
  RGB Strip LED: A tri-color Strip LED with red, green and blue. Pin order: red - common cathode - blue - green
