# Fritzing sketch A4 schematic (saved by Fritzing 0.9.3b)
breadboards: 1

parts:
  Part1 = Arduino Uno (Rev3)
  R1 = Photocell (LDR) [package=THT]
  R2 = Resistor [tolerance=±5% resistance=220 package=THT]
  R3 = Resistor [tolerance=±5% resistance=220 package=THT]
  Q1 = NPN-Transistor [package="TO92 [THT]"]
  RGB_Strip_LED2 = RGB Strip LED

nets:
  N1: Part1.A0, R1.pin_1, R2.Pin_0
  N2: Part1.D9_PWM, R3.Pin_1
  N3: Part1.GND, R2.Pin_1, Q1.E, RGB_Strip_LED2.Green_Connect#7
  N4: Part1.5V, R1.pin_0
  N5: R3.Pin_0, Q1.B

custom parts:
  RGB Strip LED: A tri-color Strip LED with red, green and blue. Pin order: red - common cathode - blue - green
