# Fritzing sketch FinalProjectSchem (saved by Fritzing 0.9.3b)
breadboards: 1

parts:
  Part1 = Arduino Uno (Rev3)
  J1 = Piezo Speaker
  Part2 = Soil Moisture Sensor

nets:
  N1: Part1.A0, Part2.SIG
  N2: Part1.D9_PWM, J1.pin2
  5V: Part1.5V, Part2.VCC
  GND: Part1.GND, J1.pin1, Part2.GND
