# Fritzing sketch Solder (saved by Fritzing 0.9.3b)
perfboards: 1

parts:
  LED1 = smd LED [color="Red (633nm)" package="0603 [SMD]"]
  R1 = Resistor [tolerance=±5% resistance=220 package="1206 [SMD]"]

nets:
  N1: LED1.cathode, R1.Pin_1
